# Fritzing sketch breadboard_mqtt_light_2 (saved by Fritzing 0.9.3b)
breadboards: 1

parts:
  U2 = NodeMCU V3.0
  M1 = WX-DC12003 [package=THT]
  Mod1 = KY-019 5V Relay Module [package="Breakout board"]
  Wechselstrom = Lilypad Battery Connect
  LED3 = LEDs [package=led10mm]

nets:
  N1: U2.D1, Mod1.S
  N2: U2.3V3, Mod1.+
  N3: U2.GND#6, U2.GND#13, U2.GND#16, U2.GND#33, M1.DC_OUT-, Mod1.-
  N4: U2.Vin, M1.DC_OUT+
  N5: M1.IN-L, Wechselstrom.+, LED3.A
  N6: M1.IN-N, Mod1.NO, Wechselstrom.-
  N7: Mod1.Common, LED3.C

custom parts:
  NodeMCU V3.0: ESP8266 based NodeMCU
  WX-DC12003: Ac to DC power supply 110/220V in 5v 700ma or 12 V 300ma out.
  KY-019 5V Relay Module: KY-019 5V Relay module, used to control AC circuits. (Special thanks to vanepp for fixing the PCB holes and other errors)
  LEDs: LEDs Standard schematic elements and footprints for 5mm, 3mm, 1206, and 0603 sized LEDs. 5mm - Spark Fun Electronics SKU : COM-00529 (and others)
