# Fritzing sketch breadboard_mqtt_plant (saved by Fritzing 0.9.3b)
breadboards: 1

parts:
  U2 = NodeMCU V3.0
  Capacitive_Soil_Moisture_Sensor1 = DFRobot Capacitive Soil Moisture Sensor V1.0 [part_number=SEN0193]

nets:
  N1: U2.GND#6, U2.GND#13, U2.GND#16, U2.GND#33, Capacitive_Soil_Moisture_Sensor1.GND
  VIN: U2.Vin, Capacitive_Soil_Moisture_Sensor1.VCC
  N2: U2.A0, Capacitive_Soil_Moisture_Sensor1.A

custom parts:
  NodeMCU V3.0: ESP8266 based NodeMCU
  DFRobot Capacitive Soil Moisture Sensor V1.0: DFRobot Capacitive Soil Moisture Sensor V1.0 This product measures soil moisture levels by capacitive sensing, rather than resistive sensing like other types of moisture sensor. It is made of a corrosion resistant material giving it a long service life. Insert it into soil and impress your friends with the real-time soil moisture data! The product includes an on-board voltage regulator which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
