# Fritzing sketch breadboard_rgb_led (saved by Fritzing 0.9.3b)
breadboards: 1

parts:
  U2 = NodeMCU V3.0
  R1 = Resistor [tolerance=±5% resistance=220 package=THT]
  R2 = Resistor [tolerance=±5% resistance=220 package=THT]
  R3 = Resistor [tolerance=±5% resistance=220 package=THT]
  LED1 = RGB LED (com. anode, rbg) [package="5 mm [THT]"]

nets:
  N1: U2.D0, R3.Pin_1
  N2: U2.D1, R2.Pin_1
  N3: U2.D2, R1.Pin_1
  N4: U2.GND#6, U2.GND#13, U2.GND#16, U2.GND#33, LED1.common_anode
  N5: R1.Pin_0, LED1.green_cathode
  N6: R2.Pin_0, LED1.blue_cathode
  N7: R3.Pin_0, LED1.red_cathode

custom parts:
  NodeMCU V3.0: ESP8266 based NodeMCU
